# Fritzing sketch voltage_regulator (saved by Fritzing 0.8.3b)

parts:
  C1 = Ceramic Capacitor [capacitance=100nF voltage=20V package="100 mil [THT, multilayer]"]
  C3 = Electrolytic Capacitor [capacitance=1µF package="100 mil [THT, electrolytic]"]
  U1 = Voltage Regulator - 5V [part_number=L7805CV package="TO220 [THT]"]
  C2 = Electrolytic Capacitor [capacitance=1µF package="100 mil [THT, electrolytic]"]
  C4 = Ceramic Capacitor [capacitance=100nF voltage=20V package="100 mil [THT, multilayer]"]
  C5 = Electrolytic Capacitor [capacitance=1µF package="100 mil [THT, electrolytic]"]
  C6 = Electrolytic Capacitor [capacitance=1µF package="100 mil [THT, electrolytic]"]
  U2 = Voltage Regulator - 3.3V [part_number=LD33V package="TO220 [THT]"]

nets:
  N1: C1.0, C3.+, U1.output_voltage
  N2: C1.1, C3.-, U1.GND, C2.-
  N3: U1.input_voltage, C2.+
  N4: C4.0, C6.+, U2.GND
  N5: C4.1, C5.-, C6.-, U2.input_voltage
  N6: C5.+, U2.output_voltage

notes:
  5v
  3.3v
  12v
  10µ
  .1µ
  L7805CV
  LD33V
